// Digital circuit LOAD.dig as structural Verilog
module LOAD (
  input  [63:0] D,
  input  [63:0] TA,
  input  [1:0] MSZ,
  output [63:0] Dout
);

  wire [31:0] multiplexer_1_out;
  wire [63:0] _64_BITS_out;

  Multiplexer #(.Bits(32)) multiplexer_1 (.sel(TA[2]), .in_0(D[31:0]), .in_1(D[63:32]), .out(multiplexer_1_out));
  BitExtender #(.inputBits(32), .outputBits(64)) _64_BITS (.in(multiplexer_1_out), .out(_64_BITS_out));
  Multiplexer #(.Selector_Bits(2), .Bits(64)) multiplexer_2 (
    .sel(MSZ), .in_0(D), .in_1(_64_BITS_out), .in_3({64{1'b0}}), .out(Dout));  // open: in_2
endmodule
