// Digital circuit alu.dig as structural Verilog
module alu (
  input  [63:0] A,
  input  [63:0] B,
  input  [2:0] ALUOp,
  output [63:0] R
);

  wire [63:0] add_1_s, mul_1_mul, sll_out, slli_out, slr_out, srli_out, sub_1_s;

  Add #(.Bits(64)) add_1 (.a(A), .b(B), .c_i(1'b0), .s(add_1_s));  // open: c_o
  Sub #(.Bits(64)) sub_1 (.a(A), .b(B), .c_i(1'b0), .s(sub_1_s));  // open: c_o
  Mul #(.Bits(32)) mul_1 (.a(A[31:0]), .b(B[31:0]), .mul(mul_1_mul));
  BarrelShifter #(.Bits(64)) sll (.in(A), .shift(B[6:0]), .out(sll_out));
  BarrelShifter #(.Bits(64), .direction("right")) slr (.in(A), .shift(B[6:0]), .out(slr_out));
  BarrelShifter #(.Bits(64)) slli (.in(A), .shift(B[6:0]), .out(slli_out));
  BarrelShifter #(.Bits(64), .direction("right")) srli (.in(A), .shift(B[6:0]), .out(srli_out));
  Multiplexer #(.Selector_Bits(3), .Bits(64)) multiplexer_1 (
    .sel(ALUOp), .in_0(add_1_s), .in_1(sub_1_s), .in_2(mul_1_mul), .in_3(sll_out), .in_4(slr_out),
    .in_5(slli_out), .in_6(srli_out), .in_7({64{1'b0}}), .out(R));
endmodule
